// Logisim project shiftreg.circ as structural Verilog: 1 circuit, main circuit main
module main (
);

  wire clock_1_out, d_ff_1_q, d_ff_2_q, d_ff_3_q, d_ff_4_q, d_ff_5_q, d_ff_6_q, d_ff_7_q, d_ff_8_q;

  Clock clock_1 (.out(clock_1_out));
  D_Flip_Flop d_ff_1 (.D(1'b0), .clk(clock_1_out), .Q(d_ff_1_q), .reset(1'b0));  // open: Qn, preset
  LED led_1 (.in(d_ff_1_q));
  D_Flip_Flop d_ff_2 (.D(d_ff_1_q), .clk(clock_1_out), .Q(d_ff_2_q), .reset(1'b0));  // open: Qn, preset
  LED led_2 (.in(d_ff_2_q));
  LED led_3 (.in(d_ff_3_q));
  D_Flip_Flop d_ff_3 (.D(d_ff_2_q), .clk(clock_1_out), .Q(d_ff_3_q), .reset(1'b0));  // open: Qn, preset
  LED led_4 (.in(d_ff_4_q));
  D_Flip_Flop d_ff_4 (.D(d_ff_3_q), .clk(clock_1_out), .Q(d_ff_4_q), .reset(1'b0));  // open: Qn, preset
  LED led_5 (.in(d_ff_5_q));
  D_Flip_Flop d_ff_5 (.D(d_ff_4_q), .clk(clock_1_out), .Q(d_ff_5_q), .reset(1'b0));  // open: Qn, preset
  D_Flip_Flop d_ff_6 (.D(d_ff_5_q), .clk(clock_1_out), .Q(d_ff_6_q), .reset(1'b0));  // open: Qn, preset
  LED led_6 (.in(d_ff_6_q));
  D_Flip_Flop d_ff_7 (.D(d_ff_6_q), .clk(clock_1_out), .Q(d_ff_7_q), .reset(1'b0));  // open: Qn, preset
  LED led_7 (.in(d_ff_7_q));
  D_Flip_Flop d_ff_8 (.D(d_ff_7_q), .clk(clock_1_out), .Q(d_ff_8_q), .reset(1'b0));  // open: Qn, preset
  LED led_8 (.in(d_ff_8_q));
endmodule
